# Fritzing sketch MonitorController_PCB_V2 (saved by Fritzing 0.8.7b)
circuit board: 2.20353cm x 1.56776cm
circuit board: 7cm x 10cm

parts:
  ARDUINO_NANO = Arduino Nano (Rev3.0)
  POWER_12V = Power plug
  BLK-GRN/RED-BLUE = screw terminal, 4 pins
  LIMIT_HOR/VER = screw terminal, 4 pins
  SWITCH = Screw terminal - 2 pins [package=THT]
  DRV8825 = A4988 Stepper Motor Driver Carrier
  C1 = Capacitor Polarized [package=cpol-radial-10uf-25v]

nets:
  N1: ARDUINO_NANO.GND, LIMIT_HOR/VER.pin1, LIMIT_HOR/VER.pin3, SWITCH.pin1, DRV8825.GROUND#147
  N2: ARDUINO_NANO.D2, DRV8825.DIR
  N3: ARDUINO_NANO.D3, DRV8825.STEP
  N4: ARDUINO_NANO.D6, DRV8825.MS3
  N5: ARDUINO_NANO.D7, DRV8825.MS2
  N6: ARDUINO_NANO.D8, DRV8825.MS1
  N7: ARDUINO_NANO.D9, DRV8825.Enable
  N8: ARDUINO_NANO.D10, SWITCH.pin2
  N9: ARDUINO_NANO.D11/MOSI, LIMIT_HOR/VER.pin2
  N10: ARDUINO_NANO.D12/MISO, LIMIT_HOR/VER.pin4
  5V: ARDUINO_NANO.5V, DRV8825.VDD
  N11: POWER_12V.GND, DRV8825.GROUND#141, C1.-
  N12: POWER_12V.VCC, DRV8825.VMOT, C1.+
  N13: BLK-GRN/RED-BLUE.pin1, DRV8825.OUT_2B
  N14: BLK-GRN/RED-BLUE.pin2, DRV8825.OUT_2A
  N15: BLK-GRN/RED-BLUE.pin3, DRV8825.OUT_1A
  N16: BLK-GRN/RED-BLUE.pin4, DRV8825.OUT_1B
  N17: DRV8825.RESET, DRV8825.SLEEP

notes:
  MOTOR
  ROTATING MONITOR CONTROLLER
